# Fritzing sketch Pi2Setup (saved by Fritzing 0.9.2b)

parts:
  Raspberry_Pi1 = Raspberry Pi 2
  Part1 = Digital FM Radio Receiver

nets:
  3V3: Raspberry_Pi1.3v3, Part1.3.3V
  N1: Raspberry_Pi1.GPIO2, Part1.SDIO
  N2: Raspberry_Pi1.GPIO3, Part1.!SEN, Part1.SCLK
  N3: Raspberry_Pi1.GPIO22, Part1.GPIO1, Part1.!RST
  N4: Raspberry_Pi1.GPIO24, Part1.GPIO2
  GND: Raspberry_Pi1.GND, Part1.GND
